# Fritzing sketch Mobile_Water_Level_Tracker (saved by Fritzing 0.9.3b)
breadboards: 2

parts:
  Part1 = Arduino Nano (Rev3.0) (ICSP)
  BT1 = Bluetooth HC-06u [package=THT]
  R1 = Resistor [tolerance=±5% resistance=220 package="2010 [SMD]"]
  R2 = Resistor [tolerance=±5% resistance=220 package="2010 [SMD]"]
  LED1 = smd LED [color="Red (633nm)" package="1206 [SMD]"]
  Water_Level_Sensor1 = Water Level Sensor
  S1 = Toggle Switch [package=THT]

nets:
  GND: Part1.GND, BT1.GND, R1.Pin_0, R2.Pin_0, Water_Level_Sensor1.GND
  N1: Part1.D2, R1.Pin_1, S1.L2
  N2: Part1.D3, LED1.anode
  N3: Part1.D4, BT1.TXD
  N4: Part1.D5, BT1.RXD
  VCC: Part1.5V, BT1.VCC, Water_Level_Sensor1.VCC, S1.L1
  N5: Part1.A0, Water_Level_Sensor1.SIG
  N6: R2.Pin_1, LED1.cathode

notes:
  Water Level Sensor(Switch)
  Funduino Water Sensor

custom parts:
  Bluetooth HC-06u: Bluetooth HC-06 - face up, pins down 16.5mm x 37.5mm PCB
  Water Level Sensor: A water level sensor. This sensor operates at 3V to 5V. The Sig (signal) pin outputs an analogue signal that is in proportion to the amount of water in contact with the sensor.
